// Logisim project decodificadore.circ as structural Verilog: 1 circuit, main circuit main
module main (
  input  E1,
  input  E2,
  input  E3,
  input  E1_2,
  input  E2_2,
  input  ENABLE,
  input  E1_3,
  input  E2_3,
  output out_9,
  output out_10,
  output out_11,
  output out_12,
  output out_13,
  output out_14,
  output out_15,
  output out_16,
  output d0,
  output d1,
  output d2,
  output d3,
  output d0_2,
  output d1_2,
  output d2_2,
  output d3_2
);

  wire and_2_out, and_3_out, and_4_out, and_5_out, not_1_out, not_2_out, not_3_out, not_4_out, not_5_out,
       not_6_out, not_7_out;

  not not_1 (not_1_out, E1);
  not not_2 (not_2_out, E2);
  not not_3 (not_3_out, E3);
  not not_4 (not_4_out, E1_2);
  not not_5 (not_5_out, E2_2);
  not not_6 (not_6_out, E1_3);
  not not_7 (not_7_out, E2_3);
  and and_1 (out_9, E3, E2, E1);
  and and_2 (and_2_out, not_4_out, not_5_out);
  and and_3 (and_3_out, not_4_out, E2_2);
  and and_4 (and_4_out, E1_2, not_5_out);
  and and_5 (and_5_out, E2_2, E1_2);
  and and_6 (d0_2, not_6_out, not_7_out);
  and and_7 (d1_2, not_6_out, E2_3);
  and and_8 (d2_2, E1_3, not_7_out);
  and and_9 (d3_2, E2_3, E1_3);
  and and_10 (out_10, not_3_out, E2, E1);
  and and_11 (out_11, E3, not_2_out, E1);
  and and_12 (d0, and_2_out, ENABLE);
  and and_13 (d1, and_3_out, ENABLE);
  and and_14 (d2, and_4_out, ENABLE);
  and and_15 (d3, and_5_out, ENABLE);
  and and_16 (out_12, not_3_out, not_2_out, E1);
  and and_17 (out_13, E3, E2, not_1_out);
  and and_18 (out_15, E3, not_2_out, not_1_out);
  and and_19 (out_14, not_3_out, E2, E2, not_1_out);
  and and_20 (out_16, not_3_out, not_2_out, not_1_out);

  // Notes on the sheet:
  //   DECODIFICADOR 2x4 (ENABLE)
  //   DECODIFICADOR 2x4 
  //   DECODIFICADOR
  //   DECODIFICADOR 3x8
  //   DAVID RIVERA MORALES
  //   320176876
endmodule
