// Logisim project multiplexor.circ as structural Verilog: 1 circuit, main circuit main
module main (
  input  ENTRADA_1,
  input  ENTRADA_2,
  input  ENTRADA_3,
  input  ENTRADA_4,
  input  SELECTOR_1,
  input  SELECTOR_2,
  output SALIDA
);

  wire and_1_out, and_2_out, and_3_out, and_4_out, not_1_out, not_2_out;

  not not_1 (not_1_out, SELECTOR_1);
  not not_2 (not_2_out, SELECTOR_2);
  and and_1 (and_1_out, ENTRADA_1, not_1_out, not_2_out);
  and and_2 (and_2_out, ENTRADA_2, not_1_out, SELECTOR_2);
  and and_3 (and_3_out, ENTRADA_3, SELECTOR_1, not_2_out);
  and and_4 (and_4_out, ENTRADA_4, SELECTOR_1, SELECTOR_2);
  or or_1 (SALIDA, and_1_out, and_2_out, and_3_out, and_4_out);

  // Notes on the sheet:
  //   MULTIPLEXOR
  //   DAVID RIVERA MORALES
  //   320176876
endmodule
