// Logisim project sumador.circ as structural Verilog: 1 circuit, main circuit main
module main (
  input  E1,
  input  E2,
  input  Bit_de_Acarreo,
  input  in_4,
  input  in_5,
  output Suma,
  output Acarreo,
  output Suma_2,
  output Acarreo_2
);

  wire and_1_out, and_2_out, and_3_out, and_4_out, and_5_out, and_7_out, and_8_out, and_9_out, not_1_out,
       not_2_out, not_3_out, not_4_out, not_5_out, not_6_out, or_1_out;

  not not_1 (not_1_out, E2);
  not not_2 (not_2_out, E1);
  not not_3 (not_3_out, in_5);
  not not_4 (not_4_out, in_4);
  and and_1 (and_1_out, E1, not_1_out);
  and and_2 (and_2_out, not_2_out, not_2_out, E2);
  and and_3 (and_3_out, E1, E2);
  and and_4 (and_4_out, in_4, not_3_out);
  and and_5 (and_5_out, not_4_out, not_4_out, in_5);
  and and_6 (Acarreo_2, in_4, in_5);
  or or_1 (or_1_out, and_1_out, and_2_out);
  or or_2 (Suma_2, and_4_out, and_5_out);
  not not_5 (not_5_out, Bit_de_Acarreo);
  not not_6 (not_6_out, or_1_out);
  and and_7 (and_7_out, or_1_out, not_5_out);
  and and_8 (and_8_out, not_6_out, Bit_de_Acarreo);
  and and_9 (and_9_out, or_1_out, Bit_de_Acarreo);
  or or_3 (Suma, and_7_out, and_8_out);
  or or_4 (Acarreo, and_9_out, and_3_out);

  // Notes on the sheet:
  //   SUMADOR MEDIO
  //   SUMADOR
  //   SUMADOR COMPLETO
  //   DAVID RIVERA MORALES
  //   320176876
endmodule
